# Fritzing sketch ir_led_connection (saved by Fritzing 0.9.3b)

parts:
  WeMos_D1_Mini1 = WeMos D1 Mini
  R1 = Resistor [tolerance=±5% resistance=220 package=THT]
  D1 = LTE-302 [package=lte-302]

nets:
  N1: WeMos_D1_Mini1.D7, R1.Pin_1
  N2: WeMos_D1_Mini1.G, D1.C
  N3: R1.Pin_0, D1.A
